# Fritzing sketch DIP-switch (saved by Fritzing 0.9.3b)
breadboards: 1

parts:
  Onderdeel1 = Arduino Uno (Rev3) - ICSP
  SW1 = DIP SWITCH [package=dipswitch-02]

nets:
  N1: Onderdeel1.A2, SW1.1
  N2: Onderdeel1.GND, SW1.4
