# Fritzing sketch seven-segment (saved by Fritzing 0.9.3b)
breadboards: 1

parts:
  IC1 = SHIFT REGISTER [package=dil16]
  R1 = Resistor [tolerance=±5% resistance=330 package="1206 [SMD]"]
  R2 = Resistor [tolerance=±5% resistance=330 package="1206 [SMD]"]
  R3 = Resistor [tolerance=±5% resistance=330 package="1206 [SMD]"]
  R4 = Resistor [tolerance=±5% resistance=330 package="1206 [SMD]"]
  R5 = Resistor [tolerance=±5% resistance=330 package="1206 [SMD]"]
  R6 = Resistor [tolerance=±5% resistance=330 package="1206 [SMD]"]
  R7 = Resistor [tolerance=±5% resistance=330 package="1206 [SMD]"]
  DI1 = 7 Segment Display  # not connected
  Onderdeel1 = Arduino Uno (Rev3) - ICSP

nets:
  N1: IC1.QB, Onderdeel1.A0
  GND: IC1.QC, IC1.QF, IC1.QG, IC1.GND, Onderdeel1.GND
  VCC: IC1.QD, IC1.QE, IC1.VCC, Onderdeel1.5V
  N2: IC1.QH, Onderdeel1.A1
  N3: IC1.QH*, R7.Pin_0
  N4: IC1.SCL, R6.Pin_0
  N5: IC1.SCK, R5.Pin_0
  N6: IC1.RCK, R4.Pin_0
  N7: IC1.G, R3.Pin_1
  N8: IC1.SER, R2.Pin_1
  N9: IC1.QA, R1.Pin_1
